# Fritzing sketch RelayBox (saved by Fritzing 0.9.3b)

parts:
  U1 = NodeMCU V1.0
  Q1 = NPN-Transistor [package="TO92 [THT]"]
  R1 = Resistor [tolerance=±5% resistance=1k package=THT]  # not connected
  R2 = Resistor [tolerance=±5% resistance=10k package=THT]
  KY-1 = Keyes Relay [package=THT]

nets:
  N1: U1.D3, R2.Pin_0
  N2: U1.GND, Q1.E
  N3: Q1.B, KY-1.signal
  N4: Q1.C, R2.Pin_1

custom parts:
  NodeMCU V1.0: ESP8266 based NodeMCU
  Keyes Relay: The Keyes 5V relay module is suitable for SCM development, home appliance control. It uses a 5V~12V TIL control signal which can control DC / AC signal.
